# Fritzing sketch Schemat (saved by Fritzing 0.9.3b)
breadboards: 1

parts:
  Part1 = Arduino Uno (Rev3)
  Part2 = Arduino Cellular Shield
  T1 = LM34 Temperature Sensor [package="TO92 [THT]"]
  R1 = Resistor [tolerance=±5% resistance=4.7k package=THT]
  Part3 = Voltage Sensor Module

nets:
  N1: Part1.A0, Part3.OUT
  N2: Part1.D8, Part2.D8
  GND: Part1.GND, Part2.GND, T1.GND, Part3.GND
  N3: Part1.D2, T1.Vout, R1.Pin_1
  N4: Part1.D7, Part2.D7
  5V: Part1.5V, Part2.5V, T1.+Vs, R1.Pin_0
